// Logisim project arich_16.circ as structural Verilog: 1 circuit, main circuit cpu
module cpu (
  input  ABORT
);

  wire ALU_FLAG, and_1_out, and_2_out, and_3_out, and_5_out, and_6_out, and_7_out, and_8_out, and_9_out,
       and_10_out, and_11_out, and_12_out, and_13_out, and_14_out, and_16_out, bcd_to_7_segment_decoder_2_p1,
       bcd_to_7_segment_decoder_3_p1, bcd_to_7_segment_decoder_4_p1, binary_to_bcd_converter_1_p2, CLK,
       comparator_3_eq, comparator_9_eq, comparator_10_eq, comparator_11_eq, comparator_12_eq,
       comparator_13_lt, comparator_14_lt, comparator_15_eq, comparator_16_eq, comparator_18_eq,
       comparator_19_eq, comparator_21_lt, comparator_22_gt, comparator_23_eq, comparator_24_eq,
       comparator_25_lt, comparator_26_lt, comparator_27_lt, comparator_28_lt, comparator_29_lt,
       comparator_30_lt, comparator_31_eq, comparator_33_lt, comparator_35_lt, comparator_36_lt,
       decoder_1_out1, decoder_1_out2, decoder_1_out3, decoder_2_out1, decoder_2_out2, ENABLE, HALT, HALT_q,
       IS_A_IMMEDIATE, IS_B_IMMEDIATE, JUMP, LDR, nor_2_out, nor_3_out, nor_4_out, nor_5_out, nor_6_out,
       not_1_out, not_2_out, not_3_out, not_4_out, not_5_out, not_7_out, not_8_out, or_2_out, or_3_out,
       or_5_out, or_6_out, or_7_out, or_8_out, or_9_out, or_10_out, or_11_out, or_14_out, or_15_out, POP,
       pull_resistor_1_node, pull_resistor_2_node, pull_resistor_6_node, pull_resistor_7_node,
       pull_resistor_8_node, pull_resistor_17_node, pull_resistor_26_node, pull_resistor_27_node,
       pull_resistor_30_node, PUSH, RESET, STACK_OVERFLOW_FLAG, STACK_UNDERFLOW_FLAG, STR;
  wire [1:0] bit_extender_6_out, comparator_17_eq;
  wire [1:1] or_1_out;
  wire [2:0] bit_extender_7_out, bit_extender_9_out, bit_extender_10_out;
  wire [3:0] bit_extender_15_out, bit_extender_16_out, bit_extender_17_out, bit_extender_18_out,
       INSTRUCTION_LENGTH_AND_OUTPUT_POSITION_LOOKUP_TABLE_data;
  wire [4:0] adder_7_cout, and_17_out, decoder_6_out0;
  wire [7:0] bit_extender_3_out, bit_extender_4_out, bit_extender_11_out, bit_extender_12_out,
       bit_extender_13_out, bit_extender_14_out, decoder_3_out0, port_module_1_port_connections_o;
  wire [9:0] adder_3_out, bit_extender_1_out, bit_extender_5_out, INSTRUCTION_LENGTH, multiplexer_2_out, PC_q;
  wire [12:0] bit_extender_8_out;
  wire [15:0] adder_1_out, adder_2_out, adder_4_out, adder_5_out, adder_7_out, adder_8_out, and_4_out,
       and_15_out, BASE_POINTER_q, bit_extender_2_out, buffer_1_out, buffer_2_out, controlled_buffer_7_out,
       DATA_BUS_A, DATA_BUS_B, DATA_BUS_C, FLAGS_REGISTER_q, JUMP_ADDRESS, multiplexer_1_out,
       multiplexer_3_out, multiplexer_4_out, multiplexer_5_out, multiplexer_6_out, multiplexer_9_out,
       multiplexer_10_out, multiplier_1_cout, multiplier_1_out, not_6_out, OPCODE, OPERAND_A, OPERAND_B,
       OPERAND_C, or_4_out, or_13_out, PROGRAM_p2, PROGRAM_p3, PROGRAM_p4, pull_resistor_16_node, R0_q, R1_q,
       R2_q, R3_q, R4_q, R5_q, R6_q, R7_q, ram_1_dout, register_1_q, shifter_1_out, shifter_2_out,
       shifter_3_out, shifter_4_out, shifter_5_out, STACK_POINTER_q, subtractor_1_out, subtractor_2_out,
       xor_1_out;
  wire [15:1] pull_resistor_9_node;
  wire [15:3] pull_resistor_5_node;

  not not_1 (not_1_out, CLK);
  not not_2 (not_2_out, JUMP);
  Multiplexer #(.width(16)) multiplexer_1 (
    .in0(JUMP_ADDRESS), .in1(DATA_BUS_C), .out(multiplexer_1_out), .sel(not_2_out));
  Pull_Resistor pull_resistor_1 (.node(pull_resistor_1_node));
  Comparator #(.mode("unsigned"), .width(16)) comparator_1 (
    .a(OPERAND_C), .b(16'h10), .eq(pull_resistor_1_node));  // open: gt, lt
  or or_1 (or_1_out[1], POP, PUSH);
  Pull_Resistor pull_resistor_2 (.node(pull_resistor_2_node));
  Comparator #(.mode("unsigned"), .width(16)) comparator_2 (
    .a(OPERAND_C), .b(16'h11), .eq(pull_resistor_2_node));  // open: gt, lt
  or or_2 (or_2_out, JUMP, pull_resistor_1_node);
  Adder #(.width(16)) adder_1 (.a(STACK_POINTER_q), .b({16{1'b1}}), .out(adder_1_out));  // open: cin, cout
  Adder #(.width(16)) adder_2 (.a(STACK_POINTER_q), .b(16'h1), .out(adder_2_out));  // open: cin, cout
  or or_3 (or_3_out, pull_resistor_2_node, or_1_out[1], comparator_3_eq);
  and and_1 (and_1_out, or_3_out, ~RESET, not_1_out);  // AND_Gate
  Adder #(.width(10)) adder_3 (.a(PC_q), .b(INSTRUCTION_LENGTH), .out(adder_3_out));  // open: cin, cout
  Bit_Extender #(.in_width(16), .out_width(10), .\type ("zero")) bit_extender_1 (
    .in(multiplexer_1_out), .out(bit_extender_1_out));
  Comparator #(.mode("unsigned"), .width(16)) comparator_3 (
    .a(OPERAND_C), .b(16'h12), .eq(comparator_3_eq));  // open: gt, lt
  Multiplexer #(.width(10)) multiplexer_2 (
    .in0(adder_3_out), .in1(bit_extender_1_out), .out(multiplexer_2_out), .sel(or_2_out));
  D_Flip_Flop u_HALT (.D(HALT), .clk(and_2_out), .Q(HALT_q), .reset(RESET));  // open: Qn, preset
  and and_2 (and_2_out, HALT, CLK);
  Button u_RESET (.out(RESET));
  Clock clock_1 (.out(CLK));
  Multiplexer #(.select(2), .width(16)) multiplexer_3 (
    .in0(DATA_BUS_C), .in1(DATA_BUS_C), .in2(adder_1_out), .in3(adder_2_out), .out(multiplexer_3_out),
    .sel({or_1_out[1], POP}));
  Pull_Resistor pull_resistor_3 (.node(comparator_3_eq));
  and and_3 (and_3_out, comparator_3_eq, ~RESET, not_1_out);  // AND_Gate
  Adder #(.width(16)) adder_4 (.a(BASE_POINTER_q), .b(16'h1), .out(adder_4_out));  // open: cin, cout
  Register #(.width(10)) PC (.D(multiplexer_2_out), .en(ENABLE), .clk(CLK), .Q(PC_q), .clr(RESET));
  Pull_Resistor pull_resistor_4 (.node(RESET));
  nor nor_1 (ENABLE, ABORT, HALT_q);
  Register #(.width(16)) STACK_POINTER (
    .D(multiplexer_3_out), .en(ENABLE), .clk(and_1_out), .Q(STACK_POINTER_q), .clr(RESET));
  Register #(.width(16)) BASE_POINTER (
    .D(multiplexer_3_out), .en(ENABLE), .clk(and_3_out), .Q(BASE_POINTER_q), .clr(RESET));
  Comparator #(.mode("unsigned"), .width(16)) comparator_4 (
    .a(STACK_POINTER_q), .b({16{1'b1}}), .eq(STACK_OVERFLOW_FLAG));  // open: gt, lt
  Comparator #(.mode("unsigned"), .width(16)) comparator_5 (
    .a(STACK_POINTER_q), .b(adder_4_out), .eq(STACK_UNDERFLOW_FLAG));  // open: gt, lt
  Pull_Resistor pull_resistor_5 (.node({pull_resistor_5_node, STACK_UNDERFLOW_FLAG, STACK_OVERFLOW_FLAG, ALU_FLAG}));
  Pull_Resistor pull_resistor_6 (.node(pull_resistor_6_node));
  Comparator #(.width(16)) comparator_6 (.a(OPERAND_A), .b(16'h10), .eq(pull_resistor_6_node));  // open: gt, lt
  Pull_Resistor pull_resistor_7 (.node(pull_resistor_7_node));
  Comparator #(.width(16)) comparator_7 (.a(OPERAND_B), .b(16'h10), .eq(pull_resistor_7_node));  // open: gt, lt
  assign bit_extender_2_out = {{6{1'b0}}, PC_q};  // Bit_Extender bit_extender_2
  assign and_4_out = {pull_resistor_5_node, STACK_UNDERFLOW_FLAG, STACK_OVERFLOW_FLAG, ALU_FLAG} & ~FLAGS_REGISTER_q;  // AND_Gate and_4, 16 bits wide
  assign or_4_out = FLAGS_REGISTER_q | {pull_resistor_5_node, STACK_UNDERFLOW_FLAG, STACK_OVERFLOW_FLAG, ALU_FLAG};  // OR_Gate or_4, 16 bits wide
  Pull_Resistor pull_resistor_8 (.node(pull_resistor_8_node));
  Comparator #(.width(16)) comparator_8 (.a(OPERAND_C), .b(16'h13), .eq(pull_resistor_8_node));  // open: gt, lt
  not not_3 (not_3_out, CLK);
  and and_5 (and_5_out, pull_resistor_6_node, ~IS_A_IMMEDIATE);  // AND_Gate
  and and_6 (and_6_out, pull_resistor_7_node, ~IS_B_IMMEDIATE);  // AND_Gate
  assign DATA_BUS_B = and_6_out ? bit_extender_2_out : 16'bz;  // Controlled_Buffer controlled_buffer_1
  // ROM #(.addrWidth(10), .dataWidth(16), .line("quad"), .misaligned("true")) PROGRAM: pin names not known; wires that end beside it: PC_q, PROGRAM_p2, PROGRAM_p3, PROGRAM_p4
  Pull_Resistor pull_resistor_9 (.node({pull_resistor_9_node, POP}));
  or or_5 (or_5_out, and_4_out[0], and_4_out[1], and_4_out[2], and_4_out[3], and_4_out[4], and_4_out[5], and_4_out[6], and_4_out[7], and_4_out[8], and_4_out[9], and_4_out[10], and_4_out[11], and_4_out[12], and_4_out[13], and_4_out[14], and_4_out[15]);
  and and_7 (and_7_out, CLK, or_5_out);
  Multiplexer #(.width(16)) multiplexer_4 (
    .in0(or_4_out), .in1(DATA_BUS_C), .out(multiplexer_4_out), .sel(pull_resistor_8_node));
  and and_8 (and_8_out, pull_resistor_8_node, not_3_out, ~RESET);  // AND_Gate
  assign DATA_BUS_A = and_5_out ? bit_extender_2_out : 16'bz;  // Controlled_Buffer controlled_buffer_2
  Adder #(.width(16)) adder_5 (
    .a({pull_resistor_9_node, POP}), .b(STACK_POINTER_q), .out(adder_5_out));  // open: cin, cout
  or or_6 (or_6_out, and_7_out, and_8_out);
  Register #(.width(16)) FLAGS_REGISTER (
    .D(multiplexer_4_out), .en(ENABLE), .clk(or_6_out), .Q(FLAGS_REGISTER_q), .clr(RESET));
  ROM #(.dataWidth(4)) INSTRUCTION_LENGTH_AND_OUTPUT_POSITION_LOOKUP_TABLE (
    .addr(bit_extender_3_out), .data(INSTRUCTION_LENGTH_AND_OUTPUT_POSITION_LOOKUP_TABLE_data));
  Bit_Extender #(.in_width(16), .out_width(8)) bit_extender_3 (
    .in({OPCODE[15:10], IS_B_IMMEDIATE, IS_A_IMMEDIATE, OPCODE[7:0]}), .out(bit_extender_3_out));
  or or_7 (or_7_out, LDR, STR);
  assign DATA_BUS_A = comparator_9_eq ? STACK_POINTER_q : 16'bz;  // Controlled_Buffer controlled_buffer_3
  Comparator #(.width(16)) comparator_9 (.a(OPERAND_A), .b(16'h11), .eq(comparator_9_eq));  // open: gt, lt
  Pull_Resistor pull_resistor_10 (.node(comparator_9_eq));
  assign DATA_BUS_B = comparator_10_eq ? STACK_POINTER_q : 16'bz;  // Controlled_Buffer controlled_buffer_4
  Comparator #(.width(16)) comparator_10 (.a(OPERAND_B), .b(16'h11), .eq(comparator_10_eq));  // open: gt, lt
  Pull_Resistor pull_resistor_11 (.node(comparator_10_eq));
  assign DATA_BUS_A = comparator_11_eq ? BASE_POINTER_q : 16'bz;  // Controlled_Buffer controlled_buffer_5
  Comparator #(.width(16)) comparator_11 (.a(OPERAND_A), .b(16'h12), .eq(comparator_11_eq));  // open: gt, lt
  Pull_Resistor pull_resistor_12 (.node(comparator_11_eq));
  assign DATA_BUS_B = comparator_12_eq ? BASE_POINTER_q : 16'bz;  // Controlled_Buffer controlled_buffer_6
  Comparator #(.width(16)) comparator_12 (.a(OPERAND_B), .b(16'h12), .eq(comparator_12_eq));  // open: gt, lt
  Pull_Resistor pull_resistor_13 (.node(comparator_12_eq));
  assign controlled_buffer_7_out = decoder_1_out3 ? PROGRAM_p4 : 16'bz;  // Controlled_Buffer controlled_buffer_7
  Decoder #(.enable("false"), .select(2)) decoder_1 (
    .out1(decoder_1_out1), .out2(decoder_1_out2), .out3(decoder_1_out3),
    .sel(INSTRUCTION_LENGTH_AND_OUTPUT_POSITION_LOOKUP_TABLE_data[3:2]));  // open: out0
  Comparator #(.mode("unsigned")) comparator_13 (
    .a(8'h18), .b(bit_extender_4_out), .lt(comparator_13_lt));  // open: gt, eq
  Bit_Extender #(.in_width(16), .out_width(8)) bit_extender_4 (
    .in({OPCODE[15:10], IS_B_IMMEDIATE, IS_A_IMMEDIATE, OPCODE[7:0]}), .out(bit_extender_4_out));
  Comparator comparator_14 (.a(bit_extender_4_out), .b(8'h1e), .lt(comparator_14_lt));  // open: gt, eq
  Multiplexer #(.width(16)) multiplexer_5 (
    .in0(adder_5_out), .in1(DATA_BUS_A), .out(multiplexer_5_out), .sel(or_7_out));
  or or_8 (or_8_out, POP, LDR);
  or or_9 (or_9_out, PUSH, STR);
  nor nor_2 (nor_2_out, decoder_1_out1, decoder_1_out2, decoder_1_out3);
  nor nor_3 (nor_3_out, decoder_1_out2, decoder_1_out3);
  and and_9 (and_9_out, comparator_13_lt, comparator_14_lt);
  LED u_ALU_FLAG (.in(FLAGS_REGISTER_q[0]));
  LED STACK_OVERFLOW (.in(FLAGS_REGISTER_q[1]));
  LED STACK_UNDERFLOW (.in(FLAGS_REGISTER_q[2]));
  assign DATA_BUS_A = comparator_15_eq ? FLAGS_REGISTER_q : 16'bz;  // Controlled_Buffer controlled_buffer_8
  Comparator #(.width(16)) comparator_15 (.a(OPERAND_A), .b(16'h13), .eq(comparator_15_eq));  // open: gt, lt
  Pull_Resistor pull_resistor_14 (.node(comparator_15_eq));
  assign DATA_BUS_B = comparator_16_eq ? FLAGS_REGISTER_q : 16'bz;  // Controlled_Buffer controlled_buffer_9
  Comparator #(.width(16)) comparator_16 (.a(OPERAND_B), .b(16'h13), .eq(comparator_16_eq));  // open: gt, lt
  Pull_Resistor pull_resistor_15 (.node(comparator_16_eq));
  or or_10 (or_10_out, decoder_1_out1, and_9_out);
  nor nor_4 (nor_4_out, RESET, CLK);
  and and_10 (and_10_out, ~or_10_out, decoder_2_out1);  // AND_Gate
  Decoder #(.enable("false"), .select(2)) decoder_2 (
    .out1(decoder_2_out1), .out2(decoder_2_out2), .sel(bit_extender_6_out));  // open: out0, out3
  Pull_Resistor pull_resistor_16 (.node(pull_resistor_16_node));
  Multiplexer #(.width(16)) multiplexer_6 (.in0(DATA_BUS_A), .in1(DATA_BUS_B), .out(multiplexer_6_out), .sel(STR));
  assign bit_extender_5_out = {{8{1'b0}}, INSTRUCTION_LENGTH_AND_OUTPUT_POSITION_LOOKUP_TABLE_data[3:2]};  // Bit_Extender bit_extender_5
  Multiplexer #(.disabled("Z"), .enable("true"), .select(2), .width(16)) multiplexer_7 (
    .in0(pull_resistor_16_node), .in1(PROGRAM_p2), .in2(PROGRAM_p3), .in3(controlled_buffer_7_out),
    .out(OPERAND_C), .sel(bit_extender_6_out), .en(or_11_out));
  Bit_Extender #(.in_width(4), .out_width(2)) bit_extender_6 (
    .in(INSTRUCTION_LENGTH_AND_OUTPUT_POSITION_LOOKUP_TABLE_data), .out(bit_extender_6_out));
  RAM #(.addrWidth(16), .asyncread("true"), .clearpin("true"), .dataWidth(16), .\type ("nonvolatile")) ram_1 (
    .addr(multiplexer_5_out), .we(or_9_out), .oe(or_8_out), .clk(nor_4_out), .din(multiplexer_6_out),
    .dout(ram_1_dout), .clr(RESET));
  Adder #(.width(10)) adder_6 (.a(bit_extender_5_out), .b(10'h1), .out(INSTRUCTION_LENGTH));  // open: cin, cout
  nor nor_5 (nor_5_out, and_10_out, nor_2_out, IS_A_IMMEDIATE);
  nor nor_6 (nor_6_out, decoder_2_out2, nor_3_out, IS_B_IMMEDIATE);
  or or_11 (or_11_out, bit_extender_6_out[1], bit_extender_6_out[0]);
  assign DATA_BUS_A = IS_A_IMMEDIATE ? PROGRAM_p2 : 16'bz;  // Controlled_Buffer controlled_buffer_10
  assign DATA_BUS_B = IS_B_IMMEDIATE ? PROGRAM_p3 : 16'bz;  // Controlled_Buffer controlled_buffer_11
  assign OPERAND_A = nor_5_out ? PROGRAM_p2 : 16'bz;  // Controlled_Buffer controlled_buffer_12
  assign OPERAND_B = nor_6_out ? PROGRAM_p3 : 16'bz;  // Controlled_Buffer controlled_buffer_13
  Comparator #(.width(16)) comparator_17 (
    .a({OPCODE[15:10], IS_B_IMMEDIATE, IS_A_IMMEDIATE, OPCODE[7:0]}), .b(16'h20), .eq(comparator_17_eq[0]));  // open: gt, lt
  Comparator #(.width(16)) comparator_18 (
    .a({OPCODE[15:10], IS_B_IMMEDIATE, IS_A_IMMEDIATE, OPCODE[7:0]}), .b(16'h27), .eq(comparator_18_eq));  // open: gt, lt
  Comparator #(.width(16)) comparator_19 (
    .a({OPCODE[15:10], IS_B_IMMEDIATE, IS_A_IMMEDIATE, OPCODE[7:0]}), .b(16'h28), .eq(comparator_19_eq));  // open: gt, lt
  or or_12 (comparator_17_eq[1], comparator_18_eq, comparator_19_eq);
  Multiplexer #(.disabled("Z"), .select(2), .width(16)) multiplexer_8 (
    .in0(controlled_buffer_7_out), .in1(OPERAND_A), .in2(OPERAND_B), .out(JUMP_ADDRESS),
    .sel(comparator_17_eq));  // open: in3
  assign DATA_BUS_C = or_8_out ? ram_1_dout : 16'bz;  // Controlled_Buffer controlled_buffer_14
  Pull_Resistor pull_resistor_17 (.node(pull_resistor_17_node));
  Comparator #(.width(16)) comparator_20 (.a(OPERAND_C), .b(16'hf0), .eq(pull_resistor_17_node));  // open: gt, lt
  not not_4 (not_4_out, CLK);
  Bit_Extender #(.in_width(16), .out_width(3), .\type ("zero")) bit_extender_7 (
    .in(OPERAND_C), .out(bit_extender_7_out));
  Comparator #(.mode("unsigned"), .width(16)) comparator_21 (
    .a(OPERAND_C), .b(16'h10), .lt(comparator_21_lt));  // open: gt, eq
  not not_5 (not_5_out, CLK);
  and and_11 (and_11_out, pull_resistor_17_node, not_4_out, ~RESET);  // AND_Gate
  Pull_Resistor pull_resistor_18 (.node(comparator_21_lt));
  Register #(.width(16)) register_1 (.D(DATA_BUS_C), .en(ENABLE), .clk(and_11_out), .Q(register_1_q), .clr(RESET));
  and and_12 (and_12_out, comparator_21_lt, ~RESET, not_5_out);  // AND_Gate
  Decoder #(.select(3)) decoder_3 (
    .out0(decoder_3_out0[0]), .out1(decoder_3_out0[1]), .out2(decoder_3_out0[2]), .out3(decoder_3_out0[3]),
    .out4(decoder_3_out0[4]), .out5(decoder_3_out0[5]), .out6(decoder_3_out0[6]), .out7(decoder_3_out0[7]),
    .sel(bit_extender_7_out), .en(and_12_out));
  Bit_Extender #(.in_width(16), .out_width(13), .\type ("zero")) bit_extender_8 (
    .in(register_1_q), .out(bit_extender_8_out));
  LED overflow (.in(comparator_22_gt));
  Comparator #(.width(16)) comparator_22 (.a(register_1_q), .b(16'h1fff), .gt(comparator_22_gt));  // open: eq, lt
  assign DATA_BUS_A = comparator_23_eq ? register_1_q : 16'bz;  // Controlled_Buffer controlled_buffer_15
  Comparator #(.width(16)) comparator_23 (.a(OPERAND_A), .b(16'hf0), .eq(comparator_23_eq));  // open: gt, lt
  Pull_Resistor pull_resistor_19 (.node(comparator_23_eq));
  assign DATA_BUS_B = comparator_24_eq ? register_1_q : 16'bz;  // Controlled_Buffer controlled_buffer_16
  Comparator #(.width(16)) comparator_24 (.a(OPERAND_B), .b(16'hf0), .eq(comparator_24_eq));  // open: gt, lt
  Pull_Resistor pull_resistor_20 (.node(comparator_24_eq));
  Register #(.width(16)) R0 (.D(DATA_BUS_C), .en(ENABLE), .clk(decoder_3_out0[0]), .Q(R0_q), .clr(RESET));
  Register #(.width(16)) R1 (.D(DATA_BUS_C), .en(ENABLE), .clk(decoder_3_out0[1]), .Q(R1_q), .clr(RESET));
  Register #(.width(16)) R2 (.D(DATA_BUS_C), .en(ENABLE), .clk(decoder_3_out0[2]), .Q(R2_q), .clr(RESET));
  Register #(.width(16)) R3 (.D(DATA_BUS_C), .en(ENABLE), .clk(decoder_3_out0[3]), .Q(R3_q), .clr(RESET));
  Register #(.width(16)) R4 (.D(DATA_BUS_C), .en(ENABLE), .clk(decoder_3_out0[4]), .Q(R4_q), .clr(RESET));
  Register #(.width(16)) R5 (.D(DATA_BUS_C), .en(ENABLE), .clk(decoder_3_out0[5]), .Q(R5_q), .clr(RESET));
  Register #(.width(16)) R6 (.D(DATA_BUS_C), .en(ENABLE), .clk(decoder_3_out0[6]), .Q(R6_q), .clr(RESET));
  Register #(.width(16)) R7 (.D(DATA_BUS_C), .en(ENABLE), .clk(decoder_3_out0[7]), .Q(R7_q), .clr(RESET));
  _7_Segment_Display u_7_segment_display_1 ();  // open: g, f, a, b, e, d, c, dp
  _7_Segment_Display u_7_segment_display_2 ();  // open: g, f, a, b, e, d, c, dp
  // BCD_to_7_Segment_decoder bcd_to_7_segment_decoder_1: pin names not known
  // BCD_to_7_Segment_decoder bcd_to_7_segment_decoder_2: pin names not known; wires that end beside it: bcd_to_7_segment_decoder_2_p1
  // Binary_to_BCD_converter #(.binvalue(13)) binary_to_bcd_converter_1: pin names not known; wires that end beside it: bit_extender_8_out, binary_to_bcd_converter_1_p2, binary_to_bcd_converter_1_p2, bcd_to_7_segment_decoder_2_p1
  _7_Segment_Display u_7_segment_display_3 ();  // open: g, f, a, b, e, d, c, dp
  // BCD_to_7_Segment_decoder bcd_to_7_segment_decoder_3: pin names not known; wires that end beside it: bcd_to_7_segment_decoder_3_p1, bcd_to_7_segment_decoder_3_p1
  _7_Segment_Display u_7_segment_display_4 ();  // open: g, f, a, b, e, d, c, dp
  // BCD_to_7_Segment_decoder bcd_to_7_segment_decoder_4: pin names not known; wires that end beside it: bcd_to_7_segment_decoder_4_p1, bcd_to_7_segment_decoder_4_p1
  Comparator #(.width(16)) comparator_25 (.a(OPERAND_A), .b(16'h8), .lt(comparator_25_lt));  // open: gt, eq
  Bit_Extender #(.in_width(16), .out_width(3), .\type ("zero")) bit_extender_9 (
    .in(OPERAND_A), .out(bit_extender_9_out));
  Bit_Extender #(.in_width(16), .out_width(3), .\type ("zero")) bit_extender_10 (
    .in(OPERAND_B), .out(bit_extender_10_out));
  Comparator #(.width(16)) comparator_26 (.a(OPERAND_B), .b(16'h8), .lt(comparator_26_lt));  // open: gt, eq
  Multiplexer #(.disabled("Z"), .select(3), .width(16)) multiplexer_9 (
    .in0(R0_q), .in1(R1_q), .in2(R2_q), .in3(R3_q), .in4(R4_q), .in5(R5_q), .in6(R6_q), .in7(R7_q),
    .out(multiplexer_9_out), .sel(bit_extender_9_out));
  Multiplexer #(.disabled("Z"), .select(3), .width(16)) multiplexer_10 (
    .in0(R0_q), .in1(R1_q), .in2(R2_q), .in3(R3_q), .in4(R4_q), .in5(R5_q), .in6(R6_q), .in7(R7_q),
    .out(multiplexer_10_out), .sel(bit_extender_10_out));
  Pull_Resistor pull_resistor_21 (.node(comparator_26_lt));
  Pull_Resistor pull_resistor_22 (.node(comparator_25_lt));
  Pull_Resistor pull_resistor_23 (.node(multiplexer_9_out));
  Pull_Resistor pull_resistor_24 (.node(multiplexer_10_out));
  assign DATA_BUS_A = comparator_25_lt ? multiplexer_9_out : 16'bz;  // Controlled_Buffer controlled_buffer_17
  assign DATA_BUS_B = comparator_26_lt ? multiplexer_10_out : 16'bz;  // Controlled_Buffer controlled_buffer_18
  port_module port_module_1 (
    .DATA_BUS_C(DATA_BUS_C), .ADDRESS(16'hf2), .PORT_CONNECTIONS_I(port_module_1_port_connections_o),
    .OPERAND_C(OPERAND_C), .CLK(CLK), .RESET(RESET), .OPERAND_A(OPERAND_A), .ENABLE(ENABLE),
    .OPERAND_B(OPERAND_B), .PORT_CONNECTIONS_O(port_module_1_port_connections_o), .DATA_BUS_A(DATA_BUS_A),
    .DATA_BUS_B(DATA_BUS_B));  // open: PORTX_REGISTER
  LED led_1 (.in(port_module_1_port_connections_o[2]));
  LED led_2 (.in(port_module_1_port_connections_o[3]));
  LED led_3 (.in(port_module_1_port_connections_o[4]));
  LED led_4 (.in(port_module_1_port_connections_o[5]));
  Bit_Extender #(.in_width(16), .out_width(8)) bit_extender_11 (
    .in({OPCODE[15:10], IS_B_IMMEDIATE, IS_A_IMMEDIATE, OPCODE[7:0]}), .out(bit_extender_11_out));
  Bit_Extender #(.in_width(16), .out_width(8)) bit_extender_12 (
    .in({OPCODE[15:10], IS_B_IMMEDIATE, IS_A_IMMEDIATE, OPCODE[7:0]}), .out(bit_extender_12_out));
  Button BP0 (.out(port_module_1_port_connections_o[0]));
  Button BP1 (.out(port_module_1_port_connections_o[1]));
  Comparator comparator_27 (.a(8'hf), .b(bit_extender_11_out), .lt(comparator_27_lt));  // open: gt, eq
  Comparator comparator_28 (.a(bit_extender_11_out), .b(8'h20), .lt(comparator_28_lt));  // open: gt, eq
  assign buffer_1_out = DATA_BUS_A;  // Buffer buffer_1, 16 bits wide
  assign buffer_2_out = DATA_BUS_B;  // Buffer buffer_2, 16 bits wide
  Pull_Resistor pull_resistor_25 (.node(buffer_2_out));
  Comparator #(.mode("unsigned")) comparator_29 (
    .a(8'h1f), .b(bit_extender_12_out), .lt(comparator_29_lt));  // open: gt, eq
  Comparator #(.mode("unsigned")) comparator_30 (
    .a(bit_extender_12_out), .b(8'h30), .lt(comparator_30_lt));  // open: gt, eq
  Pull_Resistor pull_resistor_26 (.node(pull_resistor_26_node));
  Pull_Resistor pull_resistor_27 (.node(pull_resistor_27_node));
  Bit_Extender #(.in_width(16), .out_width(8)) bit_extender_13 (
    .in({OPCODE[15:10], IS_B_IMMEDIATE, IS_A_IMMEDIATE, OPCODE[7:0]}), .out(bit_extender_13_out));
  and and_13 (and_13_out, comparator_27_lt, comparator_28_lt);
  Pull_Resistor pull_resistor_28 (.node(buffer_1_out));
  and and_14 (and_14_out, comparator_29_lt, comparator_30_lt);
  Comparator #(.mode("unsigned"), .width(16)) comparator_31 (
    .a(DATA_BUS_A), .b(DATA_BUS_B), .gt(pull_resistor_26_node), .eq(comparator_31_eq),
    .lt(pull_resistor_27_node));
  Pull_Resistor pull_resistor_29 (.node(comparator_31_eq));
  Pull_Resistor pull_resistor_30 (.node(pull_resistor_30_node));
  Comparator #(.mode("unsigned"), .width(16)) comparator_32 (
    .a(DATA_BUS_A), .b({16{1'b0}}), .eq(pull_resistor_30_node));  // open: gt, lt
  Adder #(.width(16)) adder_7 (
    .a(buffer_1_out), .b(buffer_2_out), .out(adder_7_out), .cout(adder_7_cout[0]));  // open: cin
  Subtractor #(.width(16)) subtractor_1 (
    .a(buffer_1_out), .b(buffer_2_out), .out(subtractor_1_out), .bout(adder_7_cout[1]));  // open: bin
  Multiplier #(.width(16)) multiplier_1 (
    .a(buffer_1_out), .b(buffer_2_out), .out(multiplier_1_out), .cout(multiplier_1_cout));  // open: cin
  Adder #(.width(16)) adder_8 (.a(buffer_1_out), .b(16'h1), .out(adder_8_out), .cout(adder_7_cout[3]));  // open: cin
  Subtractor #(.width(16)) subtractor_2 (
    .a(buffer_1_out), .b(16'h1), .out(subtractor_2_out), .bout(adder_7_cout[4]));  // open: bin
  assign and_15_out = buffer_1_out & buffer_2_out;  // AND_Gate and_15, 16 bits wide
  assign or_13_out = buffer_1_out | buffer_2_out;  // OR_Gate or_13, 16 bits wide
  assign xor_1_out = buffer_1_out ^ buffer_2_out;  // XOR_Gate xor_1, 16 bits wide
  assign not_6_out = ~buffer_1_out;  // NOT_Gate not_6, 16 bits wide
  Shifter #(.width(16)) shifter_1 (.in(buffer_1_out), .\dist (buffer_2_out[3:0]), .out(shifter_1_out));
  Shifter #(.shift("lr"), .width(16)) shifter_2 (.in(buffer_1_out), .\dist (buffer_2_out[3:0]), .out(shifter_2_out));
  Shifter #(.shift("ar"), .width(16)) shifter_3 (.in(buffer_1_out), .\dist (buffer_2_out[3:0]), .out(shifter_3_out));
  Shifter #(.shift("rl"), .width(16)) shifter_4 (.in(buffer_1_out), .\dist (buffer_2_out[3:0]), .out(shifter_4_out));
  Shifter #(.shift("rr"), .width(16)) shifter_5 (.in(buffer_1_out), .\dist (buffer_2_out[3:0]), .out(shifter_5_out));
  or or_14 (or_14_out, comparator_31_eq, pull_resistor_27_node);
  or or_15 (or_15_out, pull_resistor_26_node, comparator_31_eq);
  not not_7 (not_7_out, comparator_31_eq);
  not not_8 (not_8_out, pull_resistor_30_node);
  Bit_Extender #(.in_width(16), .out_width(8)) bit_extender_14 (
    .in({OPCODE[15:10], IS_B_IMMEDIATE, IS_A_IMMEDIATE, OPCODE[7:0]}), .out(bit_extender_14_out));
  Comparator comparator_33 (.a(bit_extender_13_out), .b(8'h10), .lt(comparator_33_lt));  // open: gt, eq
  Bit_Extender #(.out_width(4)) bit_extender_15 (.in(bit_extender_13_out), .out(bit_extender_15_out));
  Comparator #(.mode("unsigned"), .width(16)) comparator_34 (
    .a(multiplier_1_cout), .b({16{1'b0}}), .gt(adder_7_cout[2]));  // open: eq, lt
  Decoder #(.select(4)) decoder_4 (
    .out2(PUSH), .out3(POP), .out4(STR), .out5(LDR), .sel(bit_extender_15_out), .en(comparator_33_lt));  // open: out0, out1, out6, out7, out8, out9, out10, out11, out12, out13, out14, out15
  Multiplexer #(.disabled("Z"), .enable("true"), .select(4), .width(16)) multiplexer_11 (
    .in1(DATA_BUS_A), .in4(DATA_BUS_A), .out(DATA_BUS_C), .sel(bit_extender_15_out), .en(comparator_33_lt));  // open: in0, in2, in3, in5, in6, in7, in8, in9, in10, in11, in12, in13, in14, in15
  Comparator #(.mode("unsigned")) comparator_35 (
    .a(8'h2f), .b(bit_extender_14_out), .lt(comparator_35_lt));  // open: gt, eq
  Comparator #(.mode("unsigned")) comparator_36 (
    .a(bit_extender_14_out), .b(8'h40), .lt(comparator_36_lt));  // open: gt, eq
  Bit_Extender #(.out_width(4)) bit_extender_16 (.in(bit_extender_14_out), .out(bit_extender_16_out));
  and and_16 (and_16_out, comparator_35_lt, comparator_36_lt);
  Multiplexer #(.disabled("Z"), .enable("true"), .select(4), .width(16)) multiplexer_12 (
    .in1(DATA_BUS_A), .in4(DATA_BUS_A), .out(DATA_BUS_C), .sel(bit_extender_16_out), .en(and_16_out));  // open: in0, in2, in3, in5, in6, in7, in8, in9, in10, in11, in12, in13, in14, in15
  Bit_Extender #(.out_width(4)) bit_extender_17 (.in(bit_extender_11_out), .out(bit_extender_17_out));
  Bit_Extender #(.out_width(4)) bit_extender_18 (.in(bit_extender_12_out), .out(bit_extender_18_out));
  Decoder #(.select(4)) decoder_5 (
    .out2(HALT), .sel(bit_extender_16_out), .en(and_16_out));  // open: out0, out1, out3, out4, out5, out6, out7, out8, out9, out10, out11, out12, out13, out14, out15
  Multiplexer #(.disabled("Z"), .enable("true"), .select(4), .width(16)) multiplexer_13 (
    .in0(adder_7_out), .in1(subtractor_1_out), .in2(multiplier_1_out), .in3(adder_8_out),
    .in4(subtractor_2_out), .in5(and_15_out), .in6(or_13_out), .in7(xor_1_out), .in8(not_6_out),
    .in9(shifter_1_out), .in10(shifter_2_out), .in11(shifter_3_out), .in12(shifter_4_out),
    .in13(shifter_5_out), .out(DATA_BUS_C), .sel(bit_extender_17_out), .en(and_13_out));  // open: in14, in15
  Decoder #(.select(4)) decoder_6 (
    .out0(decoder_6_out0[0]), .out1(decoder_6_out0[1]), .out2(decoder_6_out0[2]), .out3(decoder_6_out0[3]),
    .out4(decoder_6_out0[4]), .sel(bit_extender_17_out), .en(and_13_out));  // open: out5, out6, out7, out8, out9, out10, out11, out12, out13, out14, out15
  Multiplexer #(.enable("true"), .select(4)) multiplexer_14 (
    .in0(and_14_out), .in1(or_14_out), .in2(pull_resistor_27_node), .in3(comparator_31_eq), .in4(or_15_out),
    .in5(pull_resistor_26_node), .in6(not_7_out), .in7(not_8_out), .in8(pull_resistor_30_node), .out(JUMP),
    .sel(bit_extender_18_out), .en(and_14_out));  // open: in9, in10, in11, in12, in13, in14, in15
  assign and_17_out = decoder_6_out0 & adder_7_cout;  // AND_Gate and_17, 5 bits wide
  or or_16 (ALU_FLAG, and_17_out[0], and_17_out[1], and_17_out[2], and_17_out[3], and_17_out[4]);

  // Other names for the same wires on the sheet: OPCODE[9:8] = {IS_B_IMMEDIATE, IS_A_IMMEDIATE}

  // Notes on the sheet:
  //   ABORT: pull=up
  //   STACK REGISTERS
  //   Address
  //   contents of PROGRAM (hex, n*v repeats v):
  //   304 1 1 105 1 0 101 1 1 19 0 1 13 0 13 1 4 1 0 222 1 a 9 32
  //   FLAG REGISTER
  //   contents of INSTRUCTION_LENGTH_AND_OUTPUT_POSITION_LOOKUP_TABLE (hex, n*v repeats v):
  //   0 a 4 5 8 a 10*0 f f f 5 5 f f f 5 5*9 0 0 4 6*c 8 8 7*0 5 4
  //   instructions SHL -> ROR 
  //   leur addr d'output est la meme que l'addr
  //   d'input donc il faut override le bloquage de l'OPA
  //   VARIABLE INSTRUCTION LENGTH DECODER
  //   RANDOM ACCESS MEMORY
  //   instructions JMP, IFNZ et IFZ 
  //   leurs addresses de saut sont en 1ere pos pour JMP
  //   Address
  //   et 2nde pour IFNZ et IFZ, il faut donc muxer
  //   GENERAL PURPOSE REGISTERS
  //   SMALL 7-SEG DISPLAY
  //   PORTB
  //   MOV 0x01
  //   STR 0x04
  //   GENERAL INSTRUCTIONS
  //   MOV 0x01
  //   STR 0x04
  //   ARITHMETIC AND LOGIC UNIT
  //   COMPARAISON UNIT
  //   CONTROL INSTRUCTIONS
endmodule
