// Logisim project port.circ as structural Verilog: 2 circuits, main circuit port_module
module port_module (
  input  [15:0] DATA_BUS_C,
  input  [15:0] ADDRESS,
  input  [7:0] PORT_CONNECTIONS_I,
  input  [15:0] OPERAND_C,
  input  CLK,
  input  RESET,
  input  [15:0] OPERAND_A,
  input  ENABLE,
  input  [15:0] OPERAND_B,
  output [7:0] PORTX_REGISTER,
  output [7:0] PORT_CONNECTIONS_O,
  output [15:0] DATA_BUS_A,
  output [15:0] DATA_BUS_B
);

  wire and_1_out, comparator_1_eq, comparator_2_eq, comparator_3_eq, comparator_4_eq, nor_1_out;
  wire [7:0] bit_extender_1_out, bitwise_controlled_buffer_8_1_out_3, DDRX_q, multiplexer_1_out, not_1_out;
  wire [15:0] adder_1_out, bit_extender_2_out;

  Adder #(.width(16)) adder_1 (.a(ADDRESS), .b(16'h1), .out(adder_1_out));  // open: cin, cout
  Bit_Extender #(.in_width(16), .out_width(8)) bit_extender_1 (.in(DATA_BUS_C), .out(bit_extender_1_out));
  Comparator #(.width(16)) comparator_1 (.a(OPERAND_C), .b(adder_1_out), .eq(comparator_1_eq));  // open: gt, lt
  Comparator #(.width(16)) comparator_2 (.a(OPERAND_C), .b(ADDRESS), .eq(comparator_2_eq));  // open: gt, lt
  and and_1 (and_1_out, comparator_1_eq, ~CLK, ~RESET);  // AND_Gate
  Multiplexer #(.width(8)) multiplexer_1 (
    .in0(PORTX_REGISTER), .in1(bit_extender_1_out), .out(multiplexer_1_out), .sel(comparator_2_eq));
  bitwise_controlled_buffer_8 bitwise_controlled_buffer_8_1 (
    .in_2(multiplexer_1_out), .in_1(DDRX_q), .out_3(bitwise_controlled_buffer_8_1_out_3));
  assign not_1_out = ~DDRX_q;  // NOT_Gate not_1, 8 bits wide
  bitwise_controlled_buffer_8 bitwise_controlled_buffer_8_2 (
    .in_2(PORT_CONNECTIONS_I), .in_1(not_1_out), .out_3(bitwise_controlled_buffer_8_1_out_3));
  nor nor_1 (nor_1_out, CLK, RESET);
  Register DDRX (.D(bit_extender_1_out), .en(ENABLE), .clk(and_1_out), .Q(DDRX_q), .clr(RESET));
  Register PORTX (
    .D(bitwise_controlled_buffer_8_1_out_3), .en(ENABLE), .clk(nor_1_out), .Q(PORTX_REGISTER), .clr(RESET));
  Pull_Resistor pull_resistor_1 (.node(PORT_CONNECTIONS_I));
  bitwise_controlled_buffer_8 bitwise_controlled_buffer_8_3 (
    .in_2(PORTX_REGISTER), .in_1(DDRX_q), .out_3(PORT_CONNECTIONS_O));
  assign bit_extender_2_out = {{8{1'b0}}, PORTX_REGISTER};  // Bit_Extender bit_extender_2
  Comparator #(.width(16)) comparator_3 (.a(OPERAND_A), .b(ADDRESS), .eq(comparator_3_eq));  // open: gt, lt
  Comparator #(.width(16)) comparator_4 (.a(OPERAND_B), .b(ADDRESS), .eq(comparator_4_eq));  // open: gt, lt
  assign DATA_BUS_A = comparator_3_eq ? bit_extender_2_out : 16'bz;  // Controlled_Buffer controlled_buffer_1
  Pull_Resistor pull_resistor_2 (.node(comparator_3_eq));
  assign DATA_BUS_B = comparator_4_eq ? bit_extender_2_out : 16'bz;  // Controlled_Buffer controlled_buffer_2
  Pull_Resistor pull_resistor_3 (.node(comparator_4_eq));
endmodule

module bitwise_controlled_buffer_8 (
  input  [7:0] in_1,
  input  [7:0] in_2,
  output [7:0] out_3
);

  Pull_Resistor pull_resistor_1 (.node(in_1));
  assign out_3[6] = in_1[6] ? in_2[6] : 1'bz;  // Controlled_Buffer controlled_buffer_1
  assign out_3[7] = in_1[7] ? in_2[7] : 1'bz;  // Controlled_Buffer controlled_buffer_2
  assign out_3[3] = in_1[3] ? in_2[3] : 1'bz;  // Controlled_Buffer controlled_buffer_3
  assign out_3[4] = in_1[4] ? in_2[4] : 1'bz;  // Controlled_Buffer controlled_buffer_4
  assign out_3[5] = in_1[5] ? in_2[5] : 1'bz;  // Controlled_Buffer controlled_buffer_5
  assign out_3[1] = in_1[1] ? in_2[1] : 1'bz;  // Controlled_Buffer controlled_buffer_6
  assign out_3[2] = in_1[2] ? in_2[2] : 1'bz;  // Controlled_Buffer controlled_buffer_7
  assign out_3[0] = in_1[0] ? in_2[0] : 1'bz;  // Controlled_Buffer controlled_buffer_8

  // Notes on the sheet:
  //   in_1: pull=down
endmodule
